// Logisim project 4343.circ as structural Verilog: 1 circuit, main circuit main
module main (
  input  in_1,
  input  in_2,
  input  in_3,
  input  in_4
);

  wire and_1_out, and_2_out, and_3_out, and_4_out, and_5_out, and_6_out, and_7_out, and_8_out, not_1_out,
       not_2_out, not_3_out, not_4_out, or_1_out, or_2_out, xor_1_out, xor_2_out;

  not not_1 (not_1_out, in_1);
  not not_2 (not_2_out, in_2);
  and and_1 (and_1_out, not_1_out, in_2, in_3);
  and and_2 (and_2_out, in_1, in_2);
  and and_3 (and_3_out, not_2_out, in_1, in_4);
  xor xor_1 (xor_1_out, in_2, in_4);
  xor xor_2 (xor_2_out, in_3, in_4);
  not not_3 (not_3_out, in_4);
  not not_4 (not_4_out, in_2);
  and and_4 (and_4_out, and_2_out, xor_2_out);
  and and_5 (and_5_out, not_3_out, not_4_out);
  or or_1 (or_1_out, and_1_out, and_4_out, and_3_out);
  and and_6 (and_6_out, in_2, in_4);
  or or_2 (or_2_out, and_5_out, xor_1_out);
  and and_7 (and_7_out, in_1, in_3, or_2_out);
  and and_8 (and_8_out, in_3, in_2, in_1, in_4);
  LED led_1 (.in(and_8_out));
  LED led_2 (.in(and_7_out));
  LED led_3 (.in(or_1_out));
  LED led_4 (.in(and_6_out));
endmodule
